# Fritzing sketch circuit (saved by Fritzing 0.9.3b)
breadboards: 1

parts:
  부품2 = 0.56" 7-segment LED Backpack [part_number=878]
  J1 = Piezo Speaker
  LED1 = LED - 5mm [color="Red (633nm)" package="5 mm [THT]"]
  LED2 = LED - 5mm [color="Red (633nm)" package="5 mm [THT]"]
  LED3 = LED - 5mm [color="Red (633nm)" package="5 mm [THT]"]
  LED4 = LED - 5mm [color="Red (633nm)" package="5 mm [THT]"]
  LED5 = LED - 5mm [color="Red (633nm)" package="5 mm [THT]"]
  LED6 = LED - 5mm [color="Red (633nm)" package="5 mm [THT]"]
  VCC1 = 4 x AAA Battery Mount
  부품3 = Arduino Nano (Rev3.0)
  R1 = Resistor [tolerance=±5% resistance=220 package=THT]
  R2 = Resistor [tolerance=±5% resistance=220 package=THT]
  R3 = Resistor [tolerance=±5% resistance=220 package=THT]
  R4 = Resistor [tolerance=±5% resistance=220 package=THT]
  R5 = Resistor [tolerance=±5% resistance=220 package=THT]
  R6 = Resistor [tolerance=±5% resistance=220 package=THT]

nets:
  N1: 부품2.SCL, 부품3.D3
  N2: 부품2.SDA, 부품3.D2
  GND: 부품2.GND, J1.pin1, LED1.cathode, LED2.cathode, LED3.cathode, LED4.cathode, LED5.cathode, LED6.cathode, VCC1.-, 부품3.GND
  VDD: 부품2.VDD, VCC1.+, 부품3.VIN
  N3: J1.pin2, 부품3.D4
  N4: LED1.anode, R6.Pin_0
  N5: LED2.anode, R1.Pin_0
  N6: LED4.anode, R4.Pin_0
  N7: LED5.anode, R5.Pin_0
  N8: LED6.anode, R2.Pin_0
  N9: 부품3.D6, R1.Pin_1
  N10: 부품3.D7, R2.Pin_1
  N11: 부품3.D8, R3.Pin_1
  N12: 부품3.A5, R4.Pin_1
  N13: 부품3.A4, R5.Pin_1
  N14: 부품3.A3, R6.Pin_1

custom parts:
  0.56" 7-segment LED Backpack: This 0.56" 7-segment LED display includes a driver chip for simple control via an I2C interface. The backpack features address-selection jumpers so you can connect up to eight displays on a single I2C bus.
